# Fritzing sketch TwoButtonLEDBrightness (saved by Fritzing 0.9.2b)
breadboards: 1

parts:
  R1 = Resistor [tolerance=±5% resistance=220 package=THT]
  S1 = Pushbutton [package="[THT]"]
  S2 = Pushbutton [package="[THT]"]
  LED1 = LED - 5mm [color="Red (633nm)" package="5 mm [THT]"]
  Part1 = Arduino Uno (Rev3) - ICSP
  R2 = Resistor [tolerance=±5% resistance=10k package="1206 [SMD]"]
  R3 = Resistor [tolerance=±5% resistance=10k package="1206 [SMD]"]

nets:
  N1: R1.Pin_0, LED1.anode
  N2: R1.Pin_1, Part1.ICSP_MOSI, Part1.D11_PWM/MOSI
  N3: S1.Pin_1, S1.Pin_2, Part1.D3_PWM, R2.Pin_0
  N4: S1.Pin_3, S1.Pin_4, S2.Pin_3, S2.Pin_4, Part1.5V
  N5: S2.Pin_1, S2.Pin_2, Part1.D2, R3.Pin_0
  N6: LED1.cathode, Part1.GND, R2.Pin_1, R3.Pin_1

// code stored in the sketch: TwobButtonLEDBrightness.ino

